# Fritzing sketch Project I (saved by Fritzing 0.9.3b)
breadboards: 1

parts:
  Part1 = Arduino Uno (Rev3)  # not connected
  Part2 = Arduino Motor Shield (Rev3)
  T1 = LM35 Temperature Sensor [package="TO92 [THT]"]
  M1 = DC Motor
  M2 = DC Motor
  J1 = Basic Servo
  LCD1 = LCD screen
  hc-sr1 = hc-sr04
  R1 = Trimmer Potentiometer [maximum_resistance=10kΩ package=THT]
  R2 = Resistor [tolerance=±5% resistance=220 package=THT]
  U1 = HALL-EFFECT [package=sc70]
  U2 = HALL-EFFECT [package=sc70]
  R3 = Resistor [tolerance=±5% resistance=220 package=THT]
  R4 = Resistor [tolerance=±5% resistance=220 package=THT]
  Q1 = PHOTOTRANSISTOR REFLECTIVE OBJECT SENSOR [package=qrb1114-side]
  R5 = Resistor [tolerance=±5% resistance=150 package=THT]
  R6 = Resistor [tolerance=±5% resistance=10k package=THT]
  VCC1 = 4 x AAA Battery Mount
  Part3 = Bluetooth Mate Silver

nets:
  VCC: Part2.5V, T1.+Vs, J1.vcc, LCD1.VDD, hc-sr1.VCC, R1.leg2, R2.Pin_0, U1.VCC, U2.VCC, R5.Pin_0, R6.Pin_0, Part3.VCC
  N1: Part2.A0, T1.Vout
  N2: Part2.A1, Q1.C, R6.Pin_1
  N3: Part2.A2, LCD1.DB4
  N4: Part2.A3, LCD1.DB5
  N5: Part2.A4, LCD1.DB6
  N6: Part2.A5, LCD1.DB7
  N7: Part2.D9/BreakeA, U2.OUT
  N8: Part2.D10_PWM, U1.OUT
  N9: Part2.D11_PWM/B, J1.pulse
  N10: Part2.D12/DirA, hc-sr1.Echo
  N11: Part2.D13/DirB, hc-sr1.Trig
  GND: Part2.GND, T1.GND, J1.gnd, LCD1.VSS, LCD1.R/W, LCD1.LED-, hc-sr1.GND, R1.leg1, R3.Pin_1, R4.Pin_1, Q1.E, Q1.K, VCC1.-, Part3.GND
  N12: Part2.IOREF, Part3.RX_5V
  N13: Part2.D1/TX, Part3.TX_5V
  N14: Part2.D2, LCD1.RS
  N15: Part2.D3_PWM/A, LCD1.E
  N16: Part2.B-, M1.pin_2
  N17: Part2.B+, M1.pin_1
  N18: Part2.A-, M2.pin_2
  N19: Part2.A+, M2.pin_1
  N20: Part2.VMOT, VCC1.+
  N21: LCD1.V0, R1.wiper
  N22: LCD1.LED+, R2.Pin_1
  N23: U1.GND, R3.Pin_0
  N24: U2.GND, R4.Pin_0
  N25: Q1.A, R5.Pin_1
